# Fritzing sketch Motor test (saved by Fritzing 0.9.4)

parts:
  元件1 = Arduino Uno (Rev3)
  元件2 = MD10C R2
  M1 = DC Motor
  U1 = LIPO-2000mAh [package=lipo-2000]

nets:
  N1: 元件1.D2, 元件2.no_name_yet#connector_1
  N2: 元件1.D3_PWM, 元件2.no_name_yet#connector_2
  N3: 元件1.GND, 元件2.no_name_yet#connector_3
  N4: 元件2.no_name_yet#connectorA-3, M1.pin_2
  N5: 元件2.no_name_yet#connectorB-4, M1.pin_1
  N6: 元件2.no_name_yet#connectornegative-2, U1.-
  N7: 元件2.no_name_yet#connectorpositive-1, U1.+
